# Fritzing sketch 328p programming (saved by Fritzing 0.9.3b)
breadboards: 1

parts:
  U1 = atmega328 [package=dip]
  JP1 = Header 4 [package=molex-1x4_lock]
  Y1 = CRYSTAL [package=hc49us]
  C1 = Ceramic Capacitor [capacitance=100nF package="200 mil [THT, multilayer]"]
  C2 = Ceramic Capacitor [capacitance=100nF package="200 mil [THT, multilayer]"]
  R1 = Resistor [tolerance=±5% resistance=10k package="1206 [SMD]"]

nets:
  N1: U1.RESET, U1.GND#7, U1.AVCC, JP1.3, C1.0, C2.0, R1.Pin_0
  N2: U1.D0_(RX), JP1.1
  N3: U1.D1_(TX), JP1.2
  N4: U1.VCC, U1.D12, U1.D13, JP1.4, R1.Pin_1
  N5: U1.XLAT1, Y1.2, C1.1
  N6: U1.XLAT2, Y1.1, C2.1
