# Fritzing sketch FEHBET3H0FLJF0U (saved by Fritzing 0.6.5b)
breadboards: 1

parts:
  R1 = Resistor [tolerance=±5% resistance=5k package=THT]
  R2 = Resistor [tolerance=±5% resistance=5k package=THT]
  R3 = Resistor [tolerance=±5% resistance=5k package=THT]
  Arduino1 = Arduino
  S1 = Pushbutton [package="[THT]"]
  S2 = Pushbutton [package="[THT]"]
  S3 = Pushbutton [package="[THT]"]
  S4 = Pushbutton [package="[THT]"]
  S5 = Pushbutton [package="[THT]"]
  S6 = Pushbutton [package="[THT]"]
  S7 = Pushbutton [package="[THT]"]
  S8 = Pushbutton [package="[THT]"]
  S9 = Pushbutton [package="[THT]"]
  D1 = Rectifier Diode [part_number=1N4148 package="300 mil [THT]"]
  D2 = Rectifier Diode [part_number=1N4148 package="300 mil [THT]"]
  D3 = Rectifier Diode [part_number=1N4148 package="300 mil [THT]"]
  D5 = Rectifier Diode [part_number=1N4148 package="300 mil [THT]"]
  D6 = Rectifier Diode [part_number=1N4148 package="300 mil [THT]"]
  D7 = Rectifier Diode [part_number=1N4148 package="300 mil [THT]"]
  D8 = Rectifier Diode [part_number=1N4148 package="300 mil [THT]"]
  D9 = Rectifier Diode [part_number=1N4148 package="300 mil [THT]"]
  D4 = Rectifier Diode [part_number=1N4148 package="300 mil [THT]"]

nets:
  N1: R1.Pin_0, R2.Pin_0, R3.Pin_0, Arduino1.+5V
  N2: R1.Pin_1, Arduino1.A0, S7.Pin_1, S7.Pin_2, S8.Pin_1, S8.Pin_2, S9.Pin_1, S9.Pin_2
  N3: R2.Pin_1, Arduino1.A1, S4.Pin_1, S4.Pin_2, S5.Pin_1, S5.Pin_2, S6.Pin_1, S6.Pin_2
  N4: R3.Pin_1, Arduino1.A2, S1.Pin_1, S1.Pin_2, S2.Pin_1, S2.Pin_2, S3.Pin_1, S3.Pin_2
  N5: Arduino1.D10, D1.cathode, D7.cathode, D4.cathode
  N6: Arduino1.D9, D2.cathode, D5.cathode, D8.cathode
  N7: Arduino1.D8, D3.cathode, D6.cathode, D9.cathode
  N8: S1.Pin_3, S1.Pin_4, D1.anode
  N9: S2.Pin_3, S2.Pin_4, D2.anode
  N10: S3.Pin_3, S3.Pin_4, D3.anode
  N11: S4.Pin_3, S4.Pin_4, D4.anode
  N12: S5.Pin_3, S5.Pin_4, D5.anode
  N13: S6.Pin_3, S6.Pin_4, D6.anode
  N14: S7.Pin_3, S7.Pin_4, D7.anode
  N15: S8.Pin_3, S8.Pin_4, D9.anode
  N16: S9.Pin_3, S9.Pin_4, D8.anode
