# Fritzing sketch glitcher (saved by Fritzing 0.9.3b)
breadboards: 1

parts:
  R1 = Resistor [tolerance=±5% resistance=2.2k package=THT]
  D1 = Rectifier Diode [part_number=1N4001 package="300 mil [THT]"]
  S1 = Pushbutton [package="[THT]"]
  D2 = Rectifier Diode [part_number=1N4001 package="300 mil [THT]"]
  D3 = Rectifier Diode [part_number=1N4001 package="300 mil [THT]"]
  D4 = Rectifier Diode [part_number=1N4001 package="300 mil [THT]"]
  D5 = Rectifier Diode [part_number=1N4001 package="300 mil [THT]"]
  D6 = Rectifier Diode [part_number=1N4001 package="300 mil [THT]"]
  D7 = Rectifier Diode [part_number=1N4001 package="300 mil [THT]"]
  D8 = Rectifier Diode [part_number=1N4001 package="300 mil [THT]"]
  D9 = Rectifier Diode [part_number=1N4001 package="300 mil [THT]"]
  S2 = Pushbutton [package="[THT]"]
  S3 = Pushbutton [package="[THT]"]
  S4 = Pushbutton [package="[THT]"]
  S5 = Pushbutton [package="[THT]"]
  S6 = Pushbutton [package="[THT]"]
  S7 = Pushbutton [package="[THT]"]
  S8 = Pushbutton [package="[THT]"]
  S9 = Pushbutton [package="[THT]"]
  R2 = Resistor [tolerance=±5% resistance=2.2k package=THT]
  R3 = Resistor [tolerance=±5% resistance=2.2k package=THT]
  U1 = atmega328 [package=dip]
  R4 = Resistor [tolerance=±5% resistance=4.7k package=THT]
  R5 = Resistor [tolerance=±5% resistance=1k package=THT]
  LED1 = LED - 5mm [color="Red (633nm)" package="5 mm [THT]"]
  LED2 = LED - 5mm [color="Red (633nm)" package="5 mm [THT]"]
  S10 = Toggle Switch [package=THT]
  S11 = Toggle Switch [package=THT]
  R6 = Resistor [tolerance=±5% resistance=2.2k package=THT]
  R7 = Resistor [tolerance=±5% resistance=2.2k package=THT]
  R8 = Rotary Potentiometer (Small) [maximum_resistance=100kΩ package=THT]
  R9 = Resistor [tolerance=±5% resistance=22k package=THT]
  R10 = Resistor [tolerance=±5% resistance=10k package=THT]
  R11 = Resistor [tolerance=±5% resistance=10k package=THT]
  R12 = Resistor [tolerance=±5% resistance=22k package=THT]
  R13 = Resistor [tolerance=±5% resistance=10k package=THT]
  R14 = Resistor [tolerance=±5% resistance=22k package=THT]
  R15 = Resistor [tolerance=±5% resistance=10k package=THT]
  R16 = Resistor [tolerance=±5% resistance=22k package=THT]
  R17 = Resistor [tolerance=±5% resistance=10k package=THT]
  R18 = Resistor [tolerance=±5% resistance=22k package=THT]
  R19 = Resistor [tolerance=±5% resistance=10k package=THT]
  R20 = Resistor [tolerance=±5% resistance=22k package=THT]
  R21 = Resistor [tolerance=±5% resistance=10k package=THT]
  R22 = Resistor [tolerance=±5% resistance=22k package=THT]
  R23 = Resistor [tolerance=±5% resistance=10k package=THT]
  R24 = Resistor [tolerance=±5% resistance=22k package=THT]
  R25 = Resistor [tolerance=±5% resistance=10k package=THT]
  C1 = Ceramic Capacitor [capacitance=100nF package="100 mil [THT, multilayer]"]
  C2 = Ceramic Capacitor [capacitance=100nF package="100 mil [THT, multilayer]"]
  U2 = LM386 [package=dip08]
  R26 = Rotary Potentiometer (Small) [maximum_resistance=100kΩ package=THT]
  R27 = Resistor [tolerance=±5% resistance=5k package=THT]
  R28 = Resistor [tolerance=±5% resistance=20k package=THT]
  C4 = Electrolytic Capacitor [capacitance=1µF package="100 mil [THT, electrolytic]"]
  SP1 = SPEAKER [package=pcb_mount_speaker]
  C3 = Electrolytic Capacitor [capacitance=220µF voltage=10V package="100 mil [THT, electrolytic]"]

nets:
  N1: R1.Pin_0, S1.Pin_3, S1.Pin_4, S4.Pin_3, S4.Pin_4, S7.Pin_3, U1.A2
  N2: R1.Pin_1, R2.Pin_1, R3.Pin_1, U1.VCC, U1.AVCC, U1.AREF, R6.Pin_0, R7.Pin_0, R8.leg1, U2.V+
  N3: D1.cathode, D2.cathode, D3.cathode, U1.D10_(PWM)
  N4: D1.anode, S1.Pin_1, S1.Pin_2
  N5: D2.anode, S2.Pin_1, S2.Pin_2
  N6: D3.anode, S3.Pin_1, S3.Pin_2
  N7: D4.cathode, D5.cathode, D6.cathode, U1.D9_(PWM)
  N8: D4.anode, S4.Pin_1, S4.Pin_2
  N9: D5.anode, S5.Pin_1, S5.Pin_2
  N10: D6.anode, S6.Pin_1, S6.Pin_2
  N11: D7.cathode, D8.cathode, D9.cathode, U1.D8
  N12: D7.anode, S7.Pin_1, S7.Pin_2
  N13: D8.anode, S8.Pin_1, S8.Pin_2
  N14: D9.anode, S9.Pin_1, S9.Pin_2
  N15: S2.Pin_3, S2.Pin_4, S5.Pin_3, S5.Pin_4, S8.Pin_3, R2.Pin_0, U1.A1
  N16: S3.Pin_3, S3.Pin_4, S6.Pin_3, S6.Pin_4, S9.Pin_3, R3.Pin_0, U1.A0
  N17: U1.D0_(RX), R9.Pin_1
  N18: U1.D1_(TX), R12.Pin_1
  N19: U1.D2, R14.Pin_1
  N20: U1.D3_(PWM), R16.Pin_1
  N21: U1.D4, R18.Pin_1
  N22: U1.GND, LED1.cathode, LED2.cathode, R8.wiper, R11.Pin_0, C1.1, C2.1, U2.-IN, U2.V-, R26.leg1, R27.Pin_1
  N23: U1.D5_(PWM), R20.Pin_1
  N24: U1.D6_(PWM), R22.Pin_1
  N25: U1.D7, R24.Pin_1
  N26: U1.D11_(PWM), R5.Pin_0
  N27: U1.D12, R4.Pin_0
  N28: U1.A3, S11.L1
  N29: U1.A4, S10.L1
  N30: U1.A5, R8.leg2
  N31: R4.Pin_1, LED1.anode
  N32: R5.Pin_1, LED2.anode
  N33: S10.COM, R7.Pin_1
  N34: S11.COM, R6.Pin_1
  N35: R9.Pin_0, R10.Pin_1, R11.Pin_1
  N36: R10.Pin_0, R12.Pin_0, R13.Pin_1
  N37: R13.Pin_0, R14.Pin_0, R15.Pin_1
  N38: R15.Pin_0, R16.Pin_0, R17.Pin_1
  N39: R17.Pin_0, R18.Pin_0, R19.Pin_1
  N40: R19.Pin_0, R20.Pin_0, R21.Pin_1
  N41: R21.Pin_0, R22.Pin_0, R23.Pin_1
  N42: R23.Pin_0, R24.Pin_0, R25.Pin_1, C2.0
  N43: R25.Pin_0, C1.0, C3.-
  N44: U2.+IN, R27.Pin_0, R28.Pin_1
  N45: U2.OUT, C4.+
  N46: R26.wiper, SP1.+
  N47: R26.leg2, C4.-
  N48: R28.Pin_0, C3.+
